// Logisim project 161044063_Zafer ALTAY.circ as structural Verilog: 1 circuit, main circuit main
module main (
);

  wire A_out, and_3_out, and_6_out, and_7_out, and_8_out, and_9_out, and_10_out, and_11_out, and_12_out,
       and_13_out, and_14_out, and_15_out, and_16_out, and_17_out, and_18_out, and_19_out, and_20_out,
       and_21_out, and_22_out, and_23_out, and_24_out, and_25_out, and_26_out, and_27_out, and_28_out,
       and_29_out, and_30_out, and_31_out, B_out, clock_1_out, d_ff_1_q, For_Syncron_q, not_1_out, not_2_out,
       not_3_out, not_4_out, not_5_out, not_6_out, not_7_out, not_8_out, not_9_out, not_10_out, not_11_out,
       not_12_out, not_13_out, not_14_out, not_15_out, not_16_out, not_17_out, not_18_out, not_19_out,
       not_20_out, not_21_out, not_22_out, not_23_out, not_24_out, not_25_out, not_26_out, not_27_out,
       not_28_out, not_29_out, not_30_out, not_31_out, not_32_out, not_33_out, not_34_out, not_35_out,
       not_36_out, not_37_out, not_38_out, not_39_out, not_40_out, not_41_out, not_42_out, not_43_out,
       not_44_out, not_45_out, not_46_out, not_47_out, not_48_out, or_4_out, RST_out, xor_1_out, xor_2_out;
  wire [1:0] and_1_out, and_4_out, Button_Sycronizer_2_q, Button_Sycronizer_q;
  wire [2:0] Game_Register_q, or_3_out;

  Button A (.out(A_out));
  Button B (.out(B_out));
  Clock clock_1 (.out(clock_1_out));
  Button RST (.out(RST_out));
  D_Flip_Flop For_Syncron (.clk(clock_1_out), .D(A_out), .Q(For_Syncron_q));  // open: Qn, preset, en, reset
  Register #(.width(2)) Button_Sycronizer (
    .D(and_1_out), .en(1'b1), .Q(Button_Sycronizer_q), .clk(clock_1_out));  // open: clr
  D_Flip_Flop d_ff_1 (.clk(clock_1_out), .D(B_out), .Q(d_ff_1_q));  // open: Qn, preset, en, reset
  Register #(.width(2)) Button_Sycronizer_2 (
    .D(and_4_out), .en(1'b1), .Q(Button_Sycronizer_2_q), .clk(clock_1_out));  // open: clr
  xor xor_1 (xor_1_out, Button_Sycronizer_q[1], Button_Sycronizer_q[0]);
  xor xor_2 (xor_2_out, Button_Sycronizer_2_q[1], Button_Sycronizer_2_q[0]);
  not not_1 (not_1_out, Button_Sycronizer_q[1]);
  not not_2 (not_2_out, Button_Sycronizer_q[0]);
  not not_3 (not_3_out, Button_Sycronizer_q[1]);
  not not_4 (not_4_out, Button_Sycronizer_2_q[1]);
  not not_5 (not_5_out, Button_Sycronizer_2_q[0]);
  not not_6 (not_6_out, Button_Sycronizer_2_q[1]);
  and and_1 (and_1_out[0], not_1_out, not_2_out, For_Syncron_q);
  and and_2 (and_1_out[1], For_Syncron_q, xor_1_out);
  and and_3 (and_3_out, not_3_out, Button_Sycronizer_q[0]);
  and and_4 (and_4_out[0], not_4_out, not_5_out, d_ff_1_q);
  and and_5 (and_4_out[1], d_ff_1_q, xor_2_out);
  and and_6 (and_6_out, not_6_out, Button_Sycronizer_2_q[0]);
  not not_7 (not_7_out, and_6_out);
  not not_8 (not_8_out, Game_Register_q[2]);
  not not_9 (not_9_out, Game_Register_q[0]);
  not not_10 (not_10_out, and_6_out);
  not not_11 (not_11_out, Game_Register_q[1]);
  not not_12 (not_12_out, Game_Register_q[0]);
  not not_13 (not_13_out, Game_Register_q[1]);
  not not_14 (not_14_out, and_3_out);
  not not_15 (not_15_out, Game_Register_q[1]);
  not not_16 (not_16_out, Game_Register_q[1]);
  not not_17 (not_17_out, Game_Register_q[0]);
  not not_18 (not_18_out, Game_Register_q[1]);
  not not_19 (not_19_out, Game_Register_q[0]);
  not not_20 (not_20_out, and_3_out);
  not not_21 (not_21_out, Game_Register_q[0]);
  not not_22 (not_22_out, Game_Register_q[0]);
  not not_23 (not_23_out, Game_Register_q[2]);
  not not_24 (not_24_out, Game_Register_q[0]);
  not not_25 (not_25_out, Game_Register_q[2]);
  not not_26 (not_26_out, and_6_out);
  not not_27 (not_27_out, Game_Register_q[1]);
  not not_28 (not_28_out, and_3_out);
  not not_29 (not_29_out, Game_Register_q[2]);
  not not_30 (not_30_out, and_6_out);
  not not_31 (not_31_out, Game_Register_q[1]);
  not not_32 (not_32_out, and_3_out);
  not not_33 (not_33_out, Game_Register_q[1]);
  not not_34 (not_34_out, Game_Register_q[2]);
  not not_35 (not_35_out, and_3_out);
  not not_36 (not_36_out, and_3_out);
  and and_7 (and_7_out, Game_Register_q[2], not_13_out, not_14_out);
  and and_8 (and_8_out, and_6_out, Game_Register_q[2], not_15_out);
  and and_9 (and_9_out, Game_Register_q[2], not_16_out, Game_Register_q[0]);
  and and_10 (and_10_out, Game_Register_q[2], Game_Register_q[1], not_17_out);
  and and_11 (and_11_out, not_18_out, not_19_out, not_20_out, and_6_out);
  and and_12 (and_12_out, Game_Register_q[1], not_21_out, not_7_out);
  and and_13 (and_13_out, Game_Register_q[1], not_22_out, and_3_out);
  and and_14 (and_14_out, not_23_out, Game_Register_q[1], Game_Register_q[0]);
  and and_15 (and_15_out, Game_Register_q[2], Game_Register_q[1], not_24_out);
  and and_16 (and_16_out, not_25_out, Game_Register_q[0], and_3_out, not_26_out);
  and and_17 (and_17_out, Game_Register_q[2], not_27_out, Game_Register_q[0], not_28_out, and_6_out);
  and and_18 (and_18_out, not_29_out, Game_Register_q[1], Game_Register_q[0]);
  and and_19 (and_19_out, not_8_out, not_9_out, and_3_out, not_30_out);
  and and_20 (and_20_out, not_31_out, Game_Register_q[0], not_32_out, not_10_out);
  and and_21 (and_21_out, not_33_out, Game_Register_q[0], and_3_out, and_6_out);
  and and_22 (and_22_out, not_34_out, Game_Register_q[1], not_35_out, and_6_out);
  and and_23 (and_23_out, Game_Register_q[2], not_11_out, not_12_out, not_36_out, and_6_out);
  Register #(.width(3)) Game_Register (.D(or_3_out), .en(1'b1), .Q(Game_Register_q), .clk(clock_1_out), .clr(RST_out));
  LED led_1 (.in(and_27_out));
  LED led_2 (.in(and_26_out));
  or or_1 (or_3_out[2], and_7_out, and_8_out, and_9_out, and_10_out, and_11_out);
  or or_2 (or_3_out[1], and_12_out, and_13_out, and_14_out, and_15_out, and_16_out, and_17_out);
  LED led_3 (.in(and_28_out));
  LED led_4 (.in(or_4_out));
  or or_3 (or_3_out[0], and_18_out, and_19_out, and_20_out, and_21_out, and_22_out, and_23_out);
  LED led_5 (.in(and_29_out));
  LED led_6 (.in(and_31_out));
  LED led_7 (.in(and_30_out));
  not not_37 (not_37_out, Game_Register_q[0]);
  not not_38 (not_38_out, Game_Register_q[1]);
  not not_39 (not_39_out, Game_Register_q[1]);
  not not_40 (not_40_out, Game_Register_q[2]);
  not not_41 (not_41_out, Game_Register_q[0]);
  not not_42 (not_42_out, Game_Register_q[1]);
  not not_43 (not_43_out, Game_Register_q[1]);
  not not_44 (not_44_out, Game_Register_q[0]);
  and and_24 (and_24_out, Game_Register_q[1], Game_Register_q[2], Game_Register_q[0]);
  and and_25 (and_25_out, not_39_out, not_40_out, not_41_out);
  not not_45 (not_45_out, Game_Register_q[2]);
  not not_46 (not_46_out, Game_Register_q[2]);
  not not_47 (not_47_out, Game_Register_q[0]);
  not not_48 (not_48_out, Game_Register_q[2]);
  and and_26 (and_26_out, Game_Register_q[2], Game_Register_q[1], not_37_out);
  and and_27 (and_27_out, Game_Register_q[2], not_38_out, Game_Register_q[0]);
  and and_28 (and_28_out, Game_Register_q[2], not_43_out, not_44_out);
  or or_4 (or_4_out, and_24_out, and_25_out);
  and and_29 (and_29_out, not_45_out, not_42_out, Game_Register_q[0]);
  and and_30 (and_30_out, not_46_out, Game_Register_q[1], not_47_out);
  and and_31 (and_31_out, not_48_out, Game_Register_q[1], Game_Register_q[0]);

  // Notes on the sheet:
  //   s1
  //   s0
  //   s1
  //   s0
  //   a
  //   b
  //   s1
  //   s2
  //   s0
  //   n0
  //   n1
  //   n0
  //   n1
  //   a
  //   a
  //   b
  //   b
  //   s2
  //   s1
  //   s0
  //   n2
  //   n1
  //   n0
  //   s2
  //   s1
  //   s0
  //   a7
  //   a6
  //   a5
  //   a4
  //   a3
  //   a2
  //   a1
endmodule
