// Logisim project Project2.circ as structural Verilog: 1 circuit, main circuit main
module main (
  input  [15:0] A,
  input  [15:0] B,
  output [15:0] result
);

  wire clock_1_out, GO_out, main_1_lda, main_1_ldmult, main_1_ldres, main_1_sela, main_1_seld,
       main_1_selmult, main_2_eq, main_2_gt, main_2_lt;

  Button GO (.out(GO_out));
  Clock clock_1 (.out(clock_1_out));
  ControlUnit_main main_1 (
    .gt(main_2_gt), .eq(main_2_eq), .lt(main_2_lt), .go(GO_out), .CLK(clock_1_out), .selA(main_1_sela),
    .ldRes(main_1_ldres), .selD(main_1_seld), .ldA(main_1_lda), .selMult(main_1_selmult),
    .ldMult(main_1_ldmult));
  datapath_main main_2 (
    .A(A), .selA(main_1_sela), .ldA(main_1_lda), .selLoad(main_1_seld), .selMult(main_1_selmult),
    .ldMult(main_1_ldmult), .ldRes(main_1_ldres), .CLK(clock_1_out), .B(B), .gt(main_2_gt), .eq(main_2_eq),
    .lt(main_2_lt), .result(result));
endmodule
