// Logisim project ControlUnit.circ as structural Verilog: 1 circuit, main circuit main
module main (
  input  gt,
  input  eq,
  input  lt,
  input  go,
  input  CLK,
  output selA,
  output ldRes,
  output selD,
  output ldA,
  output selMult,
  output ldMult
);

  wire and_1_out, and_2_out, and_3_out, and_4_out, and_5_out, and_6_out, and_7_out, and_8_out, and_9_out,
       and_10_out, not_1_out, not_2_out, not_3_out, not_4_out, not_5_out, not_6_out;
  wire [2:0] n0_out, Reg_q;

  not not_1 (not_1_out, gt);
  not not_2 (not_2_out, eq);
  not not_3 (not_3_out, lt);
  not not_4 (not_4_out, Reg_q[2]);
  not not_5 (not_5_out, Reg_q[1]);
  not not_6 (not_6_out, Reg_q[0]);
  Register #(.width(3)) Reg (.D(n0_out), .en(1'b1), .Q(Reg_q), .clk(CLK));  // open: clr
  and and_1 (and_1_out, not_1_out, eq, not_3_out, Reg_q[1], not_4_out);
  and and_2 (and_2_out, not_4_out, Reg_q[1], Reg_q[0]);
  and and_3 (and_3_out, Reg_q[2], not_5_out, not_6_out);
  and and_4 (and_4_out, not_4_out, Reg_q[1], not_6_out, gt, not_2_out, not_3_out);
  and and_5 (and_5_out, not_4_out, not_5_out, Reg_q[0]);
  and and_6 (and_6_out, not_4_out, not_5_out, not_6_out, go);
  and and_7 (and_7_out, not_4_out, Reg_q[1], not_6_out, not_1_out, eq, not_3_out);
  and and_8 (and_8_out, not_4_out, Reg_q[1], not_6_out, gt, not_2_out, not_3_out);
  or n2 (n0_out[2], and_1_out, and_2_out);
  or n1 (n0_out[1], and_3_out, and_4_out, and_5_out);
  or n0 (n0_out[0], and_6_out, and_7_out, and_8_out);
  and u_selA (selA, not_4_out, not_5_out, Reg_q[0]);
  and u_ldRes (ldRes, Reg_q[2], not_5_out, Reg_q[0]);
  and selLoad (selD, not_4_out, Reg_q[1], Reg_q[0]);
  and and_9 (and_9_out, not_4_out, not_5_out, Reg_q[0]);
  and and_10 (and_10_out, Reg_q[2], not_5_out, not_6_out);
  and u_selMult (selMult, not_4_out, Reg_q[1], Reg_q[0]);
  and u_ldMult (ldMult, not_4_out, Reg_q[0]);
  or u_ldA (ldA, and_9_out, and_10_out);

  // Notes on the sheet:
  //   p0
  //   p2
  //   p1
endmodule
