// Logisim project DataPath.circ as structural Verilog: 1 circuit, main circuit main
module main (
  input  [15:0] A,
  input  selA,
  input  ldA,
  input  selLoad,
  input  selMult,
  input  ldMult,
  input  ldRes,
  input  CLK,
  input  [15:0] B,
  output gt,
  output eq,
  output lt,
  output [15:0] result
);

  wire comparator_1_lt, comparator_2_lt, xnor_1_out;
  wire [15:0] adder_1_out, demultiplexer_1_out0, demultiplexer_1_out1, loadRegis_q, multiplexer_1_out,
       multiplexer_2_out, multiplexer_3_out, multiplexer_4_out, multiplexer_5_out, multiplexer_6_out,
       negator_1_out, negator_2_out, negator_3_out, register_1_q, regMult_q;

  Comparator #(.width(16)) comparator_1 (.a(A), .b({16{1'b0}}), .lt(comparator_1_lt));  // open: gt, eq
  Negator #(.width(16)) negator_1 (.in(A), .out(negator_1_out));
  Multiplexer #(.width(16), .enable("false")) multiplexer_1 (
    .in0(A), .in1(negator_1_out), .out(multiplexer_1_out), .sel(comparator_1_lt));
  Comparator #(.width(16)) comparator_2 (.a(B), .b({16{1'b0}}), .lt(comparator_2_lt));  // open: gt, eq
  Negator #(.width(16)) negator_2 (.in(B), .out(negator_2_out));
  Multiplexer #(.width(16), .enable("false")) multiplexer_2 (
    .in0(demultiplexer_1_out0), .in1(multiplexer_1_out), .out(multiplexer_2_out), .sel(selA));
  Multiplexer #(.width(16), .enable("false")) multiplexer_3 (
    .in0({16{1'b0}}), .in1(demultiplexer_1_out1), .out(multiplexer_3_out), .sel(selMult));
  Multiplexer #(.width(16), .enable("false")) multiplexer_4 (
    .in0(B), .in1(negator_2_out), .out(multiplexer_4_out), .sel(comparator_2_lt));
  Register #(.width(16)) register_1 (.D(multiplexer_2_out), .en(ldA), .Q(register_1_q), .clk(CLK));  // open: clr
  Register #(.width(16)) regMult (.D(multiplexer_3_out), .en(ldMult), .Q(regMult_q), .clk(CLK));  // open: clr
  Multiplexer #(.width(16), .enable("false")) multiplexer_5 (
    .in0({16{1'b1}}), .in1(regMult_q), .out(multiplexer_5_out), .sel(selLoad));
  Multiplexer #(.width(16), .enable("false")) multiplexer_6 (
    .in0(register_1_q), .in1(multiplexer_4_out), .out(multiplexer_6_out), .sel(selLoad));
  Adder #(.width(16)) adder_1 (
    .a(multiplexer_5_out), .b(multiplexer_6_out), .out(adder_1_out), .cin(1'b0));  // open: cout
  Demultiplexer #(.width(16), .enable("false")) demultiplexer_1 (
    .out0(demultiplexer_1_out0), .out1(demultiplexer_1_out1), .in(adder_1_out), .sel(selLoad));
  Comparator #(.width(16)) comparator_3 (.a(register_1_q), .b({16{1'b0}}), .gt(gt), .eq(eq), .lt(lt));
  Register #(.width(16)) loadRegis (.D(regMult_q), .en(ldRes), .Q(loadRegis_q), .clk(CLK));  // open: clr
  Negator #(.width(16)) negator_3 (.in(loadRegis_q), .out(negator_3_out));
  Multiplexer #(.width(16), .enable("false")) multiplexer_7 (
    .in0(negator_3_out), .in1(loadRegis_q), .out(result), .sel(xnor_1_out));
  xnor xnor_1 (xnor_1_out, comparator_2_lt, comparator_1_lt);
endmodule
