// Logisim project Display.circ as structural Verilog: 1 circuit, main circuit main
module main (
  input  clk,
  input  reset,
  input  [3:0] sellll,
  output [9:0] _1,
  output [9:0] _2,
  output [9:0] _3,
  output [9:0] _4,
  output [9:0] _5,
  output [9:0] _6,
  output [9:0] _7,
  output [9:0] _8,
  output [9:0] _9,
  output [9:0] _10
);

  wire decoder_1_out1, decoder_1_out2, decoder_1_out3, decoder_1_out4, decoder_1_out5, decoder_1_out6,
       decoder_1_out7, decoder_1_out8, decoder_1_out9, decoder_1_out10;

  Decoder #(.select(4), .enable("false")) decoder_1 (
    .out1(decoder_1_out1), .out2(decoder_1_out2), .out3(decoder_1_out3), .out4(decoder_1_out4),
    .out5(decoder_1_out5), .out6(decoder_1_out6), .out7(decoder_1_out7), .out8(decoder_1_out8),
    .out9(decoder_1_out9), .out10(decoder_1_out10), .sel(sellll));  // open: out0, out11, out12, out13, out14, out15
  Register #(.width(10)) register_1 (.D({10{1'b1}}), .en(decoder_1_out1), .Q(_1), .clk(clk), .clr(reset));
  Register #(.width(10)) register_2 (.D(10'h200), .en(decoder_1_out2), .Q(_2), .clk(clk), .clr(reset));
  Register #(.width(10)) register_3 (.D(10'h200), .en(decoder_1_out3), .Q(_3), .clk(clk), .clr(reset));
  Register #(.width(10)) register_4 (.D(10'h214), .en(decoder_1_out4), .Q(_4), .clk(clk), .clr(reset));
  Register #(.width(10)) register_5 (.D(10'h214), .en(decoder_1_out5), .Q(_5), .clk(clk), .clr(reset));
  Register #(.width(10)) register_6 (.D(10'h214), .en(decoder_1_out6), .Q(_6), .clk(clk), .clr(reset));
  Register #(.width(10)) register_7 (.D(10'h3fc), .en(decoder_1_out7), .Q(_7), .clk(clk), .clr(reset));
  Register #(.width(10)) register_8 (.D(10'h14), .en(decoder_1_out8), .Q(_8), .clk(clk), .clr(reset));
  Register #(.width(10)) register_9 (.D(10'h14), .en(decoder_1_out9), .Q(_9), .clk(clk), .clr(reset));
  Register #(.width(10)) register_10 (.D(10'h14), .en(decoder_1_out10), .Q(_10), .clk(clk), .clr(reset));
endmodule
