// Logisim project FinalProjext2.circ as structural Verilog: 1 circuit, main circuit main
module main (
  input  [31:0] word1,
  input  [31:0] word2,
  input  fillYedek,
  input  \selectGüncel ,
  input  loadWord,
  input  selCountNum,
  input  loadCountNum,
  input  CLK,
  input  selBulunanHarf,
  input  CountNumLoad,
  input  loadBulunanHarf,
  input  resetI,
  input  incrementI,
  input  Reset,
  input  startII,
  input  IncrementII,
  input  startHarfAra,
  input  IncrementHarfAra,
  input  selHarf2,
  input  [7:0] harf,
  input  loadHarf,
  input  flagSelect,
  input  loadFlag,
  input  loadharff2,
  input  loadFull2,
  output [31:0] yedek1Out,
  output word_i____0,
  output [31:0] yedek2Out,
  output maxBulunan,
  output [2:0] CountNumber,
  output IoutMax,
  output [3:0] outII,
  output harf_word_harf,
  output IIMax,
  output harfAraMax,
  output flag
);

  wire and_1_out, and_2_out, and_3_out, and_4_out, and_5_out, and_6_out, and_7_out, and_8_out,
       decoder_1_out0, decoder_1_out1, decoder_1_out2, decoder_1_out3, decoder_1_out4, decoder_1_out5,
       decoder_1_out6, decoder_1_out7, decoder_2_out0, decoder_2_out1, decoder_2_out2, decoder_2_out3,
       decoder_2_out4, decoder_2_out5, decoder_2_out6, decoder_2_out7, multiplexer_1_out, multiplexer_2_out,
       or_1_out, or_2_out, or_3_out, or_4_out, or_5_out, or_6_out, or_7_out, or_8_out;
  wire [2:0] adder_1_out, counter_1_q, CountNum_q, i_q;
  wire [3:0] BulunanHarf_q;
  wire [7:0] harf1_q, harf2_q, harf3_q, harf4_q, harf5_q, harf6_q, harf7_q, harf8_q, harfAl_q,
       multiplexer_3_out, multiplexer_4_out, multiplexer_5_out, multiplexer_6_out, multiplexer_7_out,
       multiplexer_8_out, multiplexer_9_out, multiplexer_10_out, multiplexer_11_out, multiplexer_12_out,
       multiplexer_15_out, multiplexer_16_out, multiplexer_17_out, multiplexer_18_out, multiplexer_19_out,
       multiplexer_20_out, multiplexer_21_out, multiplexer_22_out, register_1_q, register_1_q_2,
       register_1_q_3, register_1_q_4, register_2_q, register_2_q_2, register_2_q_3, register_2_q_4;
  wire [31:0] hharf4_q, hharf8_q, multiplexer_13_out, multiplexer_14_out;

  Multiplexer #(.enable("false")) multiplexer_1 (.in0(1'b0), .in1(1'b1), .out(multiplexer_1_out), .sel(loadHarf));
  Comparator #(.width(4), .mode("unsigned")) comparator_1 (
    .a(BulunanHarf_q), .b(4'b1000), .eq(maxBulunan));  // open: gt, lt
  Register #(.width(32)) register_1 (
    .D(word1), .en(loadWord), .Q({register_1_q_4, register_1_q_3, register_1_q_2, register_1_q}), .clk(CLK),
    .clr(Reset));
  Register #(.width(32)) register_2 (
    .D(word2), .en(loadWord), .Q({register_2_q_4, register_2_q_3, register_2_q_2, register_2_q}), .clk(CLK),
    .clr(Reset));
  Counter #(.width(4), .max('hf), .ongoal("stay")) BulunanHarf (
    .load(selBulunanHarf), .D(4'b0000), .count(loadBulunanHarf), .Q(BulunanHarf_q), .clk(CLK), .clr(Reset));  // open: carry
  Counter #(.width(3), .max('h7), .ongoal("stay")) CountNum (
    .load(selCountNum), .D(3'b000), .count(loadCountNum), .Q(CountNum_q), .clk(CLK), .clr(Reset));  // open: carry
  Counter #(.width(3), .max('h7), .ongoal("stay")) i (
    .load(resetI), .D(3'b000), .count(incrementI), .Q(i_q), .carry(IoutMax), .clk(CLK), .clr(Reset));
  Multiplexer #(.enable("false")) multiplexer_2 (.in0(1'b0), .in1(1'b1), .out(multiplexer_2_out), .sel(flagSelect));
  Counter #(.width(4), .max('hf)) ii (
    .load(startII), .D(4'b0000), .count(IncrementII), .Q(outII), .clk(CLK), .clr(Reset));  // open: carry
  Counter #(.width(3), .max('h7)) counter_1 (
    .load(startHarfAra), .D(3'b000), .count(IncrementHarfAra), .Q(counter_1_q), .carry(harfAraMax),
    .clk(CLK), .clr(Reset));
  Register harfAl (.D(harf), .en(multiplexer_1_out), .Q(harfAl_q), .clk(CLK), .clr(Reset));
  Register #(.width(1)) u_flag (.D(multiplexer_2_out), .en(loadFlag), .Q(flag), .clk(CLK), .clr(Reset));
  Multiplexer #(.select(3), .width(8), .enable("false")) multiplexer_3 (
    .in0(register_1_q_4), .in1(register_1_q_3), .in2(register_1_q_2), .in3(register_1_q),
    .in4(register_2_q_4), .in5(register_2_q_3), .in6(register_2_q_2), .in7(register_2_q),
    .out(multiplexer_3_out), .sel(i_q));
  Comparator #(.width(4), .mode("unsigned")) comparator_2 (.a(4'b1010), .b(outII), .eq(IIMax));  // open: gt, lt
  Decoder #(.select(3), .enable("false")) decoder_1 (
    .out0(decoder_1_out0), .out1(decoder_1_out1), .out2(decoder_1_out2), .out3(decoder_1_out3),
    .out4(decoder_1_out4), .out5(decoder_1_out5), .out6(decoder_1_out6), .out7(decoder_1_out7), .sel(i_q));
  Adder #(.width(3)) adder_1 (.a(CountNum_q), .b(3'b001), .out(adder_1_out));  // open: cin, cout
  Comparator #(.mode("unsigned")) comparator_3 (
    .a({8{1'b0}}), .b(multiplexer_3_out), .eq(word_i____0));  // open: gt, lt
  Register #(.width(3)) countNumReg (.D(adder_1_out), .en(CountNumLoad), .Q(CountNumber), .clk(CLK), .clr(Reset));
  Multiplexer #(.width(8), .enable("false")) multiplexer_4 (
    .in0(8'h2a), .in1({8{1'b0}}), .out(multiplexer_4_out), .sel(word_i____0));
  Multiplexer #(.width(8), .enable("false")) multiplexer_5 (
    .in0(8'h2a), .in1({8{1'b0}}), .out(multiplexer_5_out), .sel(word_i____0));
  Multiplexer #(.width(8), .enable("false")) multiplexer_6 (
    .in0(8'h2a), .in1({8{1'b0}}), .out(multiplexer_6_out), .sel(word_i____0));
  Multiplexer #(.width(8), .enable("false")) multiplexer_7 (
    .in0(8'h2a), .in1({8{1'b0}}), .out(multiplexer_7_out), .sel(word_i____0));
  Multiplexer #(.width(8), .enable("false")) multiplexer_8 (
    .in0(8'h2a), .in1({8{1'b0}}), .out(multiplexer_8_out), .sel(word_i____0));
  Multiplexer #(.width(8), .enable("false")) multiplexer_9 (
    .in0(8'h2a), .in1({8{1'b0}}), .out(multiplexer_9_out), .sel(word_i____0));
  Multiplexer #(.width(8), .enable("false")) multiplexer_10 (
    .in0(8'h2a), .in1({8{1'b0}}), .out(multiplexer_10_out), .sel(word_i____0));
  Multiplexer #(.width(8), .enable("false")) multiplexer_11 (
    .in0(8'h2a), .in1({8{1'b0}}), .out(multiplexer_11_out), .sel(word_i____0));
  Register harf1 (.D(multiplexer_4_out), .en(decoder_1_out0), .Q(harf1_q), .clk(CLK), .clr(Reset));
  Register harf2 (.D(multiplexer_5_out), .en(decoder_1_out1), .Q(harf2_q), .clk(CLK), .clr(Reset));
  Register harf3 (.D(multiplexer_6_out), .en(decoder_1_out2), .Q(harf3_q), .clk(CLK), .clr(Reset));
  Register harf4 (.D(multiplexer_7_out), .en(decoder_1_out3), .Q(harf4_q), .clk(CLK), .clr(Reset));
  Register harf5 (.D(multiplexer_8_out), .en(decoder_1_out4), .Q(harf5_q), .clk(CLK), .clr(Reset));
  Register harf6 (.D(multiplexer_9_out), .en(decoder_1_out5), .Q(harf6_q), .clk(CLK), .clr(Reset));
  Register harf7 (.D(multiplexer_10_out), .en(decoder_1_out6), .Q(harf7_q), .clk(CLK), .clr(Reset));
  Register harf8 (.D(multiplexer_11_out), .en(decoder_1_out7), .Q(harf8_q), .clk(CLK), .clr(Reset));
  Multiplexer #(.select(3), .width(8), .enable("false")) multiplexer_12 (
    .in0(register_1_q_4), .in1(register_1_q_3), .in2(register_1_q_2), .in3(register_1_q),
    .in4(register_2_q_4), .in5(register_2_q_3), .in6(register_2_q_2), .in7(register_2_q),
    .out(multiplexer_12_out), .sel(counter_1_q));
  Comparator comparator_4 (.a(multiplexer_12_out), .b(harfAl_q), .eq(harf_word_harf));  // open: gt, lt
  Multiplexer #(.width(32), .enable("false")) multiplexer_13 (
    .in0({harf1_q, harf2_q, harf3_q, harf4_q}), .in1(hharf4_q), .out(multiplexer_13_out), .sel(\selectGüncel ));
  Multiplexer #(.width(32), .enable("false")) multiplexer_14 (
    .in0({harf5_q, harf6_q, harf7_q, harf8_q}), .in1(hharf8_q), .out(multiplexer_14_out), .sel(\selectGüncel ));
  Decoder #(.select(3), .enable("false")) decoder_2 (
    .out0(decoder_2_out0), .out1(decoder_2_out1), .out2(decoder_2_out2), .out3(decoder_2_out3),
    .out4(decoder_2_out4), .out5(decoder_2_out5), .out6(decoder_2_out6), .out7(decoder_2_out7),
    .sel(counter_1_q));
  Multiplexer #(.width(8), .enable("false")) multiplexer_15 (
    .in0(harf1_q), .in1(register_1_q_4), .out(multiplexer_15_out), .sel(selHarf2));
  Multiplexer #(.width(8), .enable("false")) multiplexer_16 (
    .in0(harf2_q), .in1(register_1_q_3), .out(multiplexer_16_out), .sel(selHarf2));
  Multiplexer #(.width(8), .enable("false")) multiplexer_17 (
    .in0(harf3_q), .in1(register_1_q_2), .out(multiplexer_17_out), .sel(selHarf2));
  Multiplexer #(.width(8), .enable("false")) multiplexer_18 (
    .in0(harf4_q), .in1(register_1_q), .out(multiplexer_18_out), .sel(selHarf2));
  Multiplexer #(.width(8), .enable("false")) multiplexer_19 (
    .in0(harf5_q), .in1(register_2_q_4), .out(multiplexer_19_out), .sel(selHarf2));
  Multiplexer #(.width(8), .enable("false")) multiplexer_20 (
    .in0(harf6_q), .in1(register_2_q_3), .out(multiplexer_20_out), .sel(selHarf2));
  Multiplexer #(.width(8), .enable("false")) multiplexer_21 (
    .in0(harf7_q), .in1(register_2_q_2), .out(multiplexer_21_out), .sel(selHarf2));
  Multiplexer #(.width(8), .enable("false")) multiplexer_22 (
    .in0(harf8_q), .in1(register_2_q), .out(multiplexer_22_out), .sel(selHarf2));
  Register #(.width(32)) yedek1 (.D(multiplexer_13_out), .en(fillYedek), .Q(yedek1Out), .clk(CLK), .clr(Reset));
  Register #(.width(32)) yedek2 (.D(multiplexer_14_out), .en(fillYedek), .Q(yedek2Out), .clk(CLK), .clr(Reset));
  Register hharf1 (.D(multiplexer_15_out), .en(or_1_out), .Q(hharf4_q[31:24]), .clk(CLK), .clr(Reset));
  Register hharf2 (.D(multiplexer_16_out), .en(or_2_out), .Q(hharf4_q[23:16]), .clk(CLK), .clr(Reset));
  Register hharf3 (.D(multiplexer_17_out), .en(or_3_out), .Q(hharf4_q[15:8]), .clk(CLK), .clr(Reset));
  Register hharf4 (.D(multiplexer_18_out), .en(or_4_out), .Q(hharf4_q[7:0]), .clk(CLK), .clr(Reset));
  Register hharf5 (.D(multiplexer_19_out), .en(or_5_out), .Q(hharf8_q[31:24]), .clk(CLK), .clr(Reset));
  Register hharf6 (.D(multiplexer_20_out), .en(or_6_out), .Q(hharf8_q[23:16]), .clk(CLK), .clr(Reset));
  Register hharf7 (.D(multiplexer_21_out), .en(or_7_out), .Q(hharf8_q[15:8]), .clk(CLK), .clr(Reset));
  Register hharf8 (.D(multiplexer_22_out), .en(or_8_out), .Q(hharf8_q[7:0]), .clk(CLK), .clr(Reset));
  and and_1 (and_1_out, decoder_2_out0, loadharff2);
  and and_2 (and_2_out, decoder_2_out1, loadharff2);
  and and_3 (and_3_out, decoder_2_out2, loadharff2);
  and and_4 (and_4_out, decoder_2_out3, loadharff2);
  and and_5 (and_5_out, decoder_2_out4, loadharff2);
  and and_6 (and_6_out, decoder_2_out5, loadharff2);
  and and_7 (and_7_out, decoder_2_out6, loadharff2);
  and and_8 (and_8_out, decoder_2_out7, loadharff2);
  or or_1 (or_1_out, and_1_out, loadFull2);
  or or_2 (or_2_out, and_2_out, loadFull2);
  or or_3 (or_3_out, and_3_out, loadFull2);
  or or_4 (or_4_out, and_4_out, loadFull2);
  or or_5 (or_5_out, and_5_out, loadFull2);
  or or_6 (or_6_out, and_6_out, loadFull2);
  or or_7 (or_7_out, and_7_out, loadFull2);
  or or_8 (or_8_out, and_8_out, loadFull2);
endmodule
