// Logisim project buttonSenc.circ as structural Verilog: 1 circuit, main circuit main
module main (
  input  \input ,
  input  clk,
  output out
);

  wire d_ff_1_q, not_1_out, not_2_out, not_3_out, xor_1_out;
  wire [1:0] and_1_out, register_1_q;

  D_Flip_Flop d_ff_1 (.clk(clk), .D(\input ), .Q(d_ff_1_q));  // open: Qn, preset, en, reset
  not not_1 (not_1_out, register_1_q[1]);
  not not_2 (not_2_out, register_1_q[0]);
  Register #(.width(2)) register_1 (.D(and_1_out), .en(1'b1), .Q(register_1_q), .clk(clk));  // open: clr
  and and_1 (and_1_out[0], not_1_out, not_2_out, d_ff_1_q);
  and and_2 (and_1_out[1], d_ff_1_q, xor_1_out);
  xor xor_1 (xor_1_out, register_1_q[0], register_1_q[1]);
  not not_3 (not_3_out, register_1_q[1]);
  and and_3 (out, not_3_out, register_1_q[0]);
endmodule
