// Logisim project cuProject2.circ as structural Verilog: 1 circuit, main circuit main
module main (
  input  go,
  input  \Başla ,
  input  word_i__0,
  input  IoutMax,
  input  IIMax,
  input  Find,
  input  harfAraMax,
  input  harf_word_harf,
  input  maxBulunan,
  input  flag,
  input  reset,
  output loadWord,
  output selCountNum,
  output selBulunanHarf,
  output resetI,
  output loadBulunanHarf,
  output startHarfAra,
  output loadCountNum,
  output lIncrementI,
  output LoadFull2,
  output fillYedek,
  output LoadHarf,
  output countNumLoad,
  output flagSelect,
  output startII,
  output loadFlag,
  output loadHarf2,
  output selHarf2,
  output selectGuncel,
  output IncrementII,
  output IncrementHarf2
);

  wire and_1_out, and_2_out, and_3_out, and_4_out, and_5_out, and_6_out, and_7_out, and_8_out, and_9_out,
       and_10_out, and_11_out, and_12_out, and_13_out, and_14_out, and_15_out, and_16_out, and_17_out,
       and_18_out, and_19_out, and_20_out, and_21_out, and_22_out, and_23_out, and_24_out, and_27_out,
       and_28_out, and_29_out, and_32_out, and_33_out, and_36_out, and_37_out, and_38_out, and_39_out,
       and_40_out, and_41_out, and_42_out, and_43_out, and_44_out, and_45_out, and_46_out, and_47_out,
       and_50_out, and_51_out, and_55_out, clk_out, not_1_out, not_2_out, not_3_out, not_4_out, not_5_out,
       not_6_out, not_7_out, not_8_out, not_9_out, not_10_out, not_11_out, not_12_out, not_13_out,
       not_14_out, not_15_out, not_16_out, not_17_out, not_18_out, not_19_out, not_20_out, not_21_out,
       not_22_out, not_23_out, not_24_out, not_25_out, not_26_out, not_27_out, not_28_out, not_29_out,
       not_30_out, not_31_out, not_32_out, not_33_out, not_34_out, not_35_out, not_36_out, not_37_out,
       not_38_out, not_39_out, not_40_out, not_41_out, not_42_out, not_43_out, not_44_out, not_45_out,
       not_46_out, not_47_out, not_48_out, not_49_out, not_50_out, not_51_out, not_52_out, not_53_out,
       not_54_out, not_55_out, not_56_out, not_57_out, not_58_out, not_59_out, not_60_out, not_61_out,
       not_62_out, not_63_out, not_64_out, not_65_out, not_66_out, not_67_out, not_68_out, not_69_out,
       not_70_out, not_71_out, not_72_out, not_73_out, not_74_out, not_75_out, not_76_out, not_77_out,
       not_78_out, not_79_out, not_80_out, not_81_out, not_82_out, not_83_out, not_84_out, not_85_out,
       not_86_out, not_87_out, not_88_out, not_89_out, not_90_out, not_91_out, not_92_out, not_93_out,
       not_94_out, not_95_out, not_96_out, not_97_out, not_98_out, not_99_out, not_100_out, not_101_out,
       not_102_out, not_103_out, not_104_out, not_105_out, not_106_out, not_107_out, not_108_out,
       not_109_out, not_110_out, not_111_out, not_112_out, not_113_out, not_114_out, not_115_out,
       not_116_out, not_117_out, not_118_out, not_119_out, not_120_out, not_121_out, not_122_out,
       not_123_out, not_124_out, not_125_out, not_126_out, not_127_out, not_128_out, not_129_out,
       not_130_out, not_131_out, not_132_out, not_133_out, not_134_out, not_135_out, not_136_out,
       not_137_out, not_138_out, not_139_out, not_140_out, not_141_out, not_142_out, not_143_out,
       not_144_out, not_145_out, not_146_out, not_147_out, not_148_out, not_149_out, not_150_out,
       not_151_out, not_152_out, not_153_out, not_154_out, not_155_out, not_156_out, ok_2_out, ok_3_out,
       ok_4_out, ok_5_out, ok_6_out, ok_7_out, ok_8_out, ok_9_out, ok_10_out, ok_11_out, ok_12_out,
       ok_13_out, ok_14_out, ok_15_out, ok_16_out, ok_17_out, ok_18_out, ok_19_out, ok_20_out, ok_21_out,
       ok_22_out, ok_23_out, ok_24_out, ok_out, or_1_out, or_2_out, or_3_out, or_4_out, or_8_out, or_9_out,
       or_10_out, or_11_out;
  wire [4:0] n0_out, register_1_q;

  Clock clk (.out(clk_out));
  not not_1 (not_1_out, harfAraMax);
  not not_2 (not_2_out, harfAraMax);
  not not_3 (not_3_out, maxBulunan);
  and and_1 (and_1_out, not_7_out, register_1_q[0]);
  not not_4 (not_4_out, register_1_q[4]);
  and ok (ok_out, not_4_out, register_1_q[3], register_1_q[2], not_5_out, not_6_out, harfAraMax);
  not not_5 (not_5_out, register_1_q[1]);
  not not_6 (not_6_out, register_1_q[0]);
  not not_7 (not_7_out, register_1_q[1]);
  not not_8 (not_8_out, register_1_q[2]);
  not not_9 (not_9_out, Find);
  Register #(.width(5)) register_1 (.D(n0_out), .en(1'b1), .Q(register_1_q), .clk(clk_out), .clr(reset));
  not not_10 (not_10_out, register_1_q[4]);
  not not_11 (not_11_out, register_1_q[3]);
  not not_12 (not_12_out, register_1_q[2]);
  and ok_2 (ok_2_out, not_10_out, not_11_out, not_12_out, not_13_out, register_1_q[0], \Başla );
  not not_13 (not_13_out, register_1_q[1]);
  and ok_3 (ok_3_out, not_10_out, not_11_out, not_12_out, register_1_q[1], not_14_out);
  not not_14 (not_14_out, register_1_q[0]);
  and ok_4 (ok_4_out, not_10_out, not_11_out, register_1_q[2], not_15_out, not_16_out, not_17_out);
  not not_15 (not_15_out, register_1_q[1]);
  not not_16 (not_16_out, register_1_q[0]);
  not not_17 (not_17_out, word_i__0);
  not not_18 (not_18_out, register_1_q[3]);
  and ok_5 (ok_5_out, register_1_q[4], not_18_out, register_1_q[2], register_1_q[1]);
  not not_19 (not_19_out, register_1_q[3]);
  and ok_6 (ok_6_out, register_1_q[4], not_19_out, register_1_q[2], not_20_out, register_1_q[0]);
  not not_20 (not_20_out, register_1_q[1]);
  not not_21 (not_21_out, register_1_q[4]);
  not not_22 (not_22_out, register_1_q[3]);
  and ok_7 (ok_7_out, not_21_out, not_22_out, register_1_q[2], register_1_q[1]);
  not not_23 (not_23_out, register_1_q[1]);
  not not_24 (not_24_out, register_1_q[3]);
  and and_2 (and_2_out, not_24_out, register_1_q[2]);
  not not_25 (not_25_out, register_1_q[2]);
  and and_3 (and_3_out, not_25_out, register_1_q[3]);
  not not_26 (not_26_out, register_1_q[4]);
  not not_27 (not_27_out, register_1_q[1]);
  not not_28 (not_28_out, register_1_q[0]);
  not not_29 (not_29_out, register_1_q[3]);
  not not_30 (not_30_out, register_1_q[2]);
  and ok_8 (ok_8_out, register_1_q[4], not_29_out, not_30_out, not_31_out, not_32_out, not_33_out);
  not not_31 (not_31_out, register_1_q[0]);
  not not_32 (not_32_out, register_1_q[1]);
  not not_33 (not_33_out, harf_word_harf);
  not not_34 (not_34_out, register_1_q[3]);
  not not_35 (not_35_out, register_1_q[2]);
  not not_36 (not_36_out, register_1_q[0]);
  and and_4 (and_4_out, not_36_out, register_1_q[1]);
  not not_37 (not_37_out, register_1_q[4]);
  and and_5 (and_5_out, register_1_q[0], not_9_out);
  not not_38 (not_38_out, register_1_q[0]);
  and and_6 (and_6_out, not_38_out, not_39_out);
  not not_39 (not_39_out, IIMax);
  not not_40 (not_40_out, register_1_q[4]);
  not not_41 (not_41_out, register_1_q[1]);
  not not_42 (not_42_out, register_1_q[2]);
  not not_43 (not_43_out, register_1_q[4]);
  not not_44 (not_44_out, register_1_q[2]);
  not not_45 (not_45_out, register_1_q[3]);
  not not_46 (not_46_out, register_1_q[0]);
  not not_47 (not_47_out, register_1_q[1]);
  not not_48 (not_48_out, register_1_q[4]);
  not not_49 (not_49_out, register_1_q[2]);
  not not_50 (not_50_out, register_1_q[3]);
  not not_51 (not_51_out, register_1_q[4]);
  not not_52 (not_52_out, register_1_q[4]);
  not not_53 (not_53_out, register_1_q[2]);
  and ok_9 (ok_9_out, not_52_out, register_1_q[3], not_53_out, not_54_out, register_1_q[1], IIMax);
  not not_54 (not_54_out, register_1_q[0]);
  not not_55 (not_55_out, register_1_q[4]);
  not not_56 (not_56_out, register_1_q[3]);
  not not_57 (not_57_out, register_1_q[0]);
  not not_58 (not_58_out, register_1_q[2]);
  not not_59 (not_59_out, register_1_q[4]);
  not not_60 (not_60_out, register_1_q[0]);
  not not_61 (not_61_out, register_1_q[1]);
  not not_62 (not_62_out, register_1_q[1]);
  not not_63 (not_63_out, register_1_q[3]);
  not not_64 (not_64_out, register_1_q[1]);
  not not_65 (not_65_out, register_1_q[2]);
  not not_66 (not_66_out, register_1_q[4]);
  or or_1 (or_1_out, and_2_out, and_3_out);
  and and_7 (and_7_out, register_1_q[0], not_27_out);
  or or_2 (or_2_out, and_7_out, and_8_out);
  and and_8 (and_8_out, register_1_q[1], not_28_out);
  and and_9 (and_9_out, register_1_q[4], not_34_out, not_35_out, or_3_out);
  or or_3 (or_3_out, and_4_out, and_1_out);
  and ok_10 (ok_10_out, not_37_out, register_1_q[3], not_8_out, register_1_q[1], or_4_out);
  or or_4 (or_4_out, and_5_out, and_6_out);
  not not_67 (not_67_out, register_1_q[4]);
  not not_68 (not_68_out, register_1_q[3]);
  not not_69 (not_69_out, register_1_q[2]);
  not not_70 (not_70_out, register_1_q[1]);
  not not_71 (not_71_out, register_1_q[0]);
  not not_72 (not_72_out, register_1_q[4]);
  not not_73 (not_73_out, register_1_q[3]);
  not not_74 (not_74_out, register_1_q[0]);
  and and_10 (and_10_out, not_40_out, register_1_q[3], register_1_q[2], not_41_out, register_1_q[0]);
  and and_11 (and_11_out, not_42_out, register_1_q[3], not_43_out);
  and and_12 (and_12_out, maxBulunan, register_1_q[0], register_1_q[1], not_44_out, not_45_out, register_1_q[4]);
  and and_13 (and_13_out, not_1_out, not_46_out, not_47_out, register_1_q[2], register_1_q[3], not_48_out);
  and and_14 (and_14_out, IoutMax, register_1_q[0], register_1_q[1], not_49_out, not_50_out, not_51_out);
  not not_75 (not_75_out, register_1_q[2]);
  not not_76 (not_76_out, register_1_q[3]);
  not not_77 (not_77_out, register_1_q[1]);
  not not_78 (not_78_out, register_1_q[4]);
  not not_79 (not_79_out, register_1_q[3]);
  not not_80 (not_80_out, register_1_q[2]);
  not not_81 (not_81_out, register_1_q[1]);
  not not_82 (not_82_out, register_1_q[0]);
  and and_15 (and_15_out, not_79_out, not_78_out, not_80_out, register_1_q[1], register_1_q[0], not_83_out);
  not not_83 (not_83_out, IoutMax);
  and and_16 (and_16_out, not_55_out, not_56_out, register_1_q[2], register_1_q[1], not_57_out);
  and and_17 (and_17_out, not_55_out, register_1_q[3], not_58_out, register_1_q[1], register_1_q[0], Find);
  and and_18 (and_18_out, not_59_out, register_1_q[3], register_1_q[2], not_60_out, not_61_out, not_2_out);
  and and_19 (and_19_out, not_59_out, register_1_q[3], register_1_q[2], not_62_out, register_1_q[0]);
  and and_20 (and_20_out, not_63_out, register_1_q[2], not_64_out);
  and and_21 (and_21_out, register_1_q[4], not_63_out, not_65_out, register_1_q[0], register_1_q[1], not_3_out);
  and and_22 (and_22_out, not_66_out, register_1_q[3], register_1_q[2], register_1_q[1]);
  and ok_11 (ok_11_out, not_21_out, not_23_out, register_1_q[0], or_1_out);
  and ok_12 (ok_12_out, not_26_out, register_1_q[3], register_1_q[2], or_2_out);
  not not_84 (not_84_out, register_1_q[0]);
  not not_85 (not_85_out, register_1_q[3]);
  not not_86 (not_86_out, register_1_q[2]);
  not not_87 (not_87_out, register_1_q[1]);
  not not_88 (not_88_out, register_1_q[2]);
  not not_89 (not_89_out, register_1_q[1]);
  not not_90 (not_90_out, register_1_q[0]);
  not not_91 (not_91_out, register_1_q[3]);
  not not_92 (not_92_out, register_1_q[2]);
  not not_93 (not_93_out, register_1_q[0]);
  not not_94 (not_94_out, register_1_q[1]);
  and and_23 (and_23_out, not_75_out, register_1_q[4], not_76_out);
  and and_24 (and_24_out, not_76_out, register_1_q[4], register_1_q[2], not_77_out);
  and ok_13 (ok_13_out, register_1_q[4], register_1_q[3], not_95_out, not_96_out);
  not not_95 (not_95_out, register_1_q[1]);
  not not_96 (not_96_out, register_1_q[2]);
  or n1 (n0_out[1], ok_2_out, ok_3_out, ok_4_out, ok_5_out, ok_6_out, and_9_out, ok_7_out, ok_11_out, ok_12_out, ok_8_out, ok_10_out);
  and and_25 (loadWord, not_67_out, not_68_out, not_69_out, not_70_out, register_1_q[0]);
  and and_26 (resetI, not_67_out, not_68_out, not_69_out, register_1_q[1], not_84_out);
  and and_27 (and_27_out, not_67_out, not_68_out, register_1_q[2], not_70_out, register_1_q[0]);
  or or_5 (loadBulunanHarf, and_27_out, and_28_out, and_29_out);
  and and_28 (and_28_out, not_67_out, register_1_q[3], register_1_q[2], register_1_q[1], not_71_out);
  and and_29 (and_29_out, register_1_q[4], not_85_out, not_86_out, not_87_out, register_1_q[0]);
  and and_30 (loadCountNum, not_72_out, not_73_out, register_1_q[2], register_1_q[1], not_74_out);
  and and_31 (lIncrementI, not_72_out, not_73_out, register_1_q[2], register_1_q[1], register_1_q[0]);
  and and_32 (and_32_out, not_72_out, register_1_q[3], not_88_out, not_89_out, not_90_out);
  and and_33 (and_33_out, register_1_q[4], not_91_out, not_92_out, register_1_q[1], not_93_out);
  and and_34 (countNumLoad, not_72_out, register_1_q[3], not_92_out, not_93_out, not_94_out);
  and and_35 (startII, not_94_out, register_1_q[0], not_92_out, register_1_q[3], not_72_out);
  or n4 (n0_out[4], ok_out, and_23_out, ok_9_out, and_24_out, ok_13_out);
  or or_6 (n0_out[2], and_15_out, and_16_out, and_17_out, and_18_out, and_19_out, and_20_out, and_21_out, and_22_out);
  or or_7 (fillYedek, and_32_out, and_33_out);
  not not_97 (not_97_out, register_1_q[3]);
  and and_36 (and_36_out, not_97_out, register_1_q[4]);
  and and_37 (and_37_out, register_1_q[4], register_1_q[3], not_98_out, not_99_out);
  not not_98 (not_98_out, register_1_q[2]);
  not not_99 (not_99_out, register_1_q[1]);
  not not_100 (not_100_out, register_1_q[4]);
  and and_38 (and_38_out, not_100_out, register_1_q[3]);
  and and_39 (and_39_out, or_8_out, register_1_q[2], register_1_q[1]);
  or or_8 (or_8_out, and_36_out, and_38_out);
  not not_101 (not_101_out, register_1_q[4]);
  not not_102 (not_102_out, register_1_q[0]);
  not not_103 (not_103_out, register_1_q[3]);
  not not_104 (not_104_out, register_1_q[2]);
  not not_105 (not_105_out, register_1_q[1]);
  not not_106 (not_106_out, register_1_q[0]);
  not not_107 (not_107_out, register_1_q[4]);
  not not_108 (not_108_out, register_1_q[2]);
  not not_109 (not_109_out, register_1_q[0]);
  not not_110 (not_110_out, register_1_q[4]);
  not not_111 (not_111_out, register_1_q[3]);
  not not_112 (not_112_out, register_1_q[3]);
  not not_113 (not_113_out, register_1_q[0]);
  not not_114 (not_114_out, register_1_q[2]);
  and and_40 (and_40_out, not_114_out, register_1_q[1]);
  and and_41 (and_41_out, register_1_q[2], not_115_out);
  not not_115 (not_115_out, register_1_q[1]);
  not not_116 (not_116_out, register_1_q[4]);
  not not_117 (not_117_out, register_1_q[3]);
  not not_118 (not_118_out, register_1_q[1]);
  not not_119 (not_119_out, register_1_q[0]);
  not not_120 (not_120_out, register_1_q[4]);
  not not_121 (not_121_out, register_1_q[3]);
  not not_122 (not_122_out, register_1_q[2]);
  not not_123 (not_123_out, register_1_q[1]);
  not not_124 (not_124_out, register_1_q[0]);
  not not_125 (not_125_out, \Başla );
  not not_126 (not_126_out, register_1_q[4]);
  not not_127 (not_127_out, register_1_q[1]);
  not not_128 (not_128_out, register_1_q[0]);
  not not_129 (not_129_out, harfAraMax);
  not not_130 (not_130_out, harf_word_harf);
  not not_131 (not_131_out, register_1_q[4]);
  not not_132 (not_132_out, register_1_q[2]);
  not not_133 (not_133_out, Find);
  not not_134 (not_134_out, register_1_q[3]);
  not not_135 (not_135_out, register_1_q[1]);
  not not_136 (not_136_out, register_1_q[2]);
  not not_137 (not_137_out, register_1_q[1]);
  not not_138 (not_138_out, register_1_q[4]);
  not not_139 (not_139_out, register_1_q[3]);
  not not_140 (not_140_out, register_1_q[2]);
  not not_141 (not_141_out, register_1_q[0]);
  not not_142 (not_142_out, register_1_q[4]);
  not not_143 (not_143_out, register_1_q[3]);
  not not_144 (not_144_out, register_1_q[1]);
  or n3 (n0_out[3], and_39_out, and_37_out, and_10_out, and_14_out, and_11_out, and_12_out, and_13_out);
  and ok_14 (ok_14_out, not_101_out, register_1_q[3], register_1_q[2], register_1_q[1], not_102_out);
  and ok_15 (ok_15_out, register_1_q[4], not_103_out, not_104_out, not_105_out, not_106_out, harf_word_harf);
  and and_42 (and_42_out, register_1_q[3], not_107_out, not_108_out, not_109_out);
  and ok_16 (ok_16_out, not_110_out, not_111_out, register_1_q[2], register_1_q[1]);
  and ok_17 (ok_17_out, register_1_q[4], not_112_out, not_113_out, or_9_out);
  or or_9 (or_9_out, and_40_out, and_41_out);
  and ok_18 (ok_18_out, not_116_out, not_117_out, not_118_out, register_1_q[2], not_119_out, word_i__0);
  and and_43 (and_43_out, not_124_out, go);
  or or_10 (or_10_out, and_43_out, and_44_out);
  and and_44 (and_44_out, register_1_q[0], not_125_out);
  and and_45 (and_45_out, not_128_out, not_129_out);
  or or_11 (or_11_out, and_45_out, and_46_out);
  and and_46 (and_46_out, register_1_q[0], not_130_out);
  and ok_19 (ok_19_out, not_131_out, register_1_q[3], not_132_out, register_1_q[1], register_1_q[0], not_133_out);
  and ok_20 (ok_20_out, register_1_q[4], not_134_out, register_1_q[2], not_135_out, register_1_q[0], flag);
  and ok_21 (ok_21_out, register_1_q[4], register_1_q[3], not_136_out, not_137_out, register_1_q[0]);
  and ok_22 (ok_22_out, not_138_out, not_139_out, not_140_out, register_1_q[1], not_141_out);
  and and_47 (and_47_out, not_142_out, not_143_out, register_1_q[2], not_144_out, register_1_q[0]);
  not not_145 (not_145_out, register_1_q[4]);
  not not_146 (not_146_out, register_1_q[2]);
  not not_147 (not_147_out, register_1_q[1]);
  not not_148 (not_148_out, register_1_q[4]);
  not not_149 (not_149_out, register_1_q[0]);
  not not_150 (not_150_out, register_1_q[3]);
  not not_151 (not_151_out, register_1_q[2]);
  not not_152 (not_152_out, register_1_q[1]);
  and ok_23 (ok_23_out, not_120_out, not_121_out, not_122_out, not_123_out, or_10_out);
  and ok_24 (ok_24_out, not_126_out, register_1_q[3], register_1_q[2], not_127_out, or_11_out);
  not not_153 (not_153_out, register_1_q[3]);
  not not_154 (not_154_out, register_1_q[2]);
  not not_155 (not_155_out, register_1_q[0]);
  not not_156 (not_156_out, register_1_q[4]);
  or n0 (n0_out[0], ok_14_out, ok_15_out, and_42_out, ok_16_out, ok_17_out, ok_18_out, and_47_out, ok_23_out, ok_24_out, ok_19_out, ok_20_out, ok_21_out, ok_22_out);
  and and_48 (LoadFull2, not_145_out, register_1_q[3], not_146_out, not_147_out, register_1_q[0]);
  and and_49 (LoadHarf, not_145_out, register_1_q[3], not_146_out, register_1_q[1], register_1_q[0]);
  and and_50 (and_50_out, not_148_out, register_1_q[3], register_1_q[2], register_1_q[1], not_149_out);
  and and_51 (and_51_out, register_1_q[4], not_150_out, not_151_out, not_152_out, register_1_q[0]);
  and and_52 (selectGuncel, register_1_q[4], not_153_out, not_154_out, register_1_q[1], not_155_out);
  and and_53 (IncrementII, register_1_q[4], not_153_out, register_1_q[1], not_155_out, register_1_q[2]);
  and and_54 (IncrementHarf2, not_156_out, register_1_q[3], register_1_q[2], register_1_q[1], register_1_q[0]);
  or or_12 (startHarfAra, LoadFull2, LoadHarf);
  or or_13 (flagSelect, and_50_out, and_51_out);
  or or_14 (loadFlag, and_50_out, and_51_out, and_55_out);
  and and_55 (and_55_out, register_1_q[4], not_150_out, register_1_q[2], register_1_q[1], register_1_q[0]);
  or or_15 (loadHarf2, and_50_out, and_51_out);

  assign selBulunanHarf = resetI;
  assign selCountNum = resetI;
  assign selHarf2 = loadHarf2;

  // Notes on the sheet:
  //   p3
  //   p2
  //   p1
  //   p1
  //   p4
  //   p0
  //   p0
  //   p4
  //   p3
  //   p2
endmodule
