// Logisim project finalProj.circ as structural Verilog: 1 circuit, main circuit main
module main (
  input  [31:0] word1,
  input  [31:0] word2,
  input  RESET_SCORE
);

  wire a_out, b_out, \başla_out , c_out, clk_out, d_out, e_out, f_out, find_out, g_out, go_out, h_out, i_out,
       j_out, k_out, l_out, m_out, main_1_out, main_2_p3, main_2_p4, main_2_p5, main_2_p7, main_2_p8,
       main_2_p9, main_2_p10, main_2_p12, main_2_p13, main_2_p14, main_2_p15, main_2_p16, main_2_p17,
       main_2_p18, main_2_p19, main_2_p20, main_2_p21, main_2_p22, main_2_p23, main_2_p24, main_2_p25,
       main_2_p26, main_2_p27, main_2_p28, main_2_p29, main_2_p30, main_2_p31, main_7_out, main_8_out,
       n7segdisp_1_a, n7segdisp_1_b, n7segdisp_1_c, n7segdisp_1_d, n7segdisp_1_e, n7segdisp_1_f,
       n7segdisp_1_g, n7segdisp_2_a, n7segdisp_2_b, n7segdisp_2_c, n7segdisp_2_d, n7segdisp_2_e,
       n7segdisp_2_f, n7segdisp_2_g, n7segdisp_3_a, n7segdisp_3_b, n7segdisp_3_c, n7segdisp_3_d,
       n7segdisp_3_e, n7segdisp_3_f, n7segdisp_3_g, n_out, o_out, p_out, q_out, r_out, reset_out, s_out,
       t_out, u_out, v_out, w_out, x_out, y_out, z_out;
  wire [2:0] counter_1_q, counter_2_q, main_4_countnumber;
  wire [3:0] main_4_outii;
  wire [6:0] bit_extender_1_out;
  wire [7:0] main_3_harf, main_5_outharf;
  wire [9:0] main_6__1, main_6__2, main_6__3, main_6__4, main_6__5, main_6__6, main_6__7, main_6__8,
       main_6__9, main_6__10;
  wire [31:0] main_4_yedek1out, main_4_yedek2out, multiplexer_1_out, multiplexer_2_out;

  Button find (.out(find_out));
  Clock clk (.out(clk_out));
  buttonSenc_main main_1 (.\input (find_out), .clk(clk_out), .out(main_1_out));
  Button reset (.out(reset_out));
  Button \başla  (.out(\başla_out ));
  Button go (.out(go_out));
  Button a (.out(a_out));
  Button b (.out(b_out));
  Button c (.out(c_out));
  Button d (.out(d_out));
  Button e (.out(e_out));
  Button f (.out(f_out));
  Button g (.out(g_out));
  Button h (.out(h_out));
  Button i (.out(i_out));
  Button j (.out(j_out));
  Button k (.out(k_out));
  Button l (.out(l_out));
  Button m (.out(m_out));
  Button n (.out(n_out));
  Button o (.out(o_out));
  Button p (.out(p_out));
  Button q (.out(q_out));
  Button r (.out(r_out));
  Button s (.out(s_out));
  Button t (.out(t_out));
  Button u (.out(u_out));
  Button v (.out(v_out));
  Button w (.out(w_out));
  Button x (.out(x_out));
  Button y (.out(y_out));
  Button z (.out(z_out));
  // cuProject2_main main_2: pin names not known; wires that end beside it: go_out, \başla_out , main_2_p3, main_2_p4, main_2_p5, main_1_out, main_2_p7, main_2_p8, main_2_p9, main_2_p10, clk_out, main_2_p12, main_2_p13, main_2_p14, main_2_p15, main_2_p16, main_2_p17, main_2_p18, main_2_p19, main_2_p20, main_2_p21, main_2_p22, main_2_p23, main_2_p24, main_2_p25, main_2_p26, main_2_p27, main_2_p28, main_2_p29, main_2_p30, main_2_p31, reset_out
  harfler_main main_3 (
    .a(a_out), .b(b_out), .c(c_out), .d(d_out), .e(e_out), .f(f_out), .g(g_out), .h(h_out), .i(i_out),
    .j(j_out), .k(k_out), .l(l_out), .m(m_out), .n(n_out), .o(o_out), .p(p_out), .q(q_out), .r(r_out),
    .s(s_out), .t(t_out), .u(u_out), .v(v_out), .w(w_out), .x(x_out), .y(y_out), .z(z_out), .clk(clk_out),
    .reset(reset_out), .harf(main_3_harf));
  FinalProjext2_main main_4 (
    .word1(word1), .word2(word2), .loadWord(main_2_p12), .selCountNum(main_2_p13), .loadCountNum(main_2_p18),
    .CLK(clk_out), .selBulunanHarf(main_2_p14), .CountNumLoad(main_2_p23), .loadBulunanHarf(main_2_p16),
    .resetI(main_2_p15), .incrementI(main_2_p19), .Reset(reset_out), .startII(main_2_p25),
    .IncrementII(main_2_p30), .startHarfAra(main_2_p17), .IncrementHarfAra(main_2_p31), .harf(main_3_harf),
    .loadHarf(main_2_p22), .flagSelect(main_2_p24), .loadFlag(main_2_p26), .selHarf2(main_2_p28),
    .\selectGüncel (main_2_p29), .fillYedek(main_2_p21), .loadharff2(main_2_p27), .loadFull2(main_2_p20),
    .yedek1Out(main_4_yedek1out), .word_i____0(main_2_p3), .yedek2Out(main_4_yedek2out),
    .maxBulunan(main_2_p9), .CountNumber(main_4_countnumber), .IoutMax(main_2_p4), .outII(main_4_outii),
    .harf_word_harf(main_2_p8), .IIMax(main_2_p5), .harfAraMax(main_2_p7), .flag(main_2_p10));
  Multiplexer #(.width(32), .enable("false")) multiplexer_1 (
    .in0(main_4_yedek1out), .in1(word1), .out(multiplexer_1_out), .sel(main_2_p5));
  TTY tty_1 (.data(bit_extender_1_out), .clk(clk_out), .clr(reset_out));  // open: we
  Multiplexer #(.width(32), .enable("false")) multiplexer_2 (
    .in0(main_4_yedek2out), .in1(word2), .out(multiplexer_2_out), .sel(main_2_p5));
  _7_Segment_Display u_7_segment_display_1 (
    .g(n7segdisp_1_g), .f(n7segdisp_1_f), .a(n7segdisp_1_a), .b(n7segdisp_1_b), .e(n7segdisp_1_e),
    .d(n7segdisp_1_d), .c(n7segdisp_1_c));  // open: dp
  _7segDisp u_7segdisp_1 (
    .in_1(main_4_countnumber), .a(n7segdisp_1_a), .b(n7segdisp_1_b), .c(n7segdisp_1_c), .d(n7segdisp_1_d),
    .e(n7segdisp_1_e), .f(n7segdisp_1_f), .g(n7segdisp_1_g));
  Bit_Extender #(.out_width(7)) bit_extender_1 (.in(main_5_outharf), .out(bit_extender_1_out));
  forTTY_main main_5 (._1(multiplexer_1_out), ._2(multiplexer_2_out), .clk(clk_out), .outHarf(main_5_outharf));
  LED led_1 (.in(main_2_p9));
  Display_main main_6 (
    .clk(clk_out), .reset(reset_out), .sellll(main_4_outii), ._1(main_6__1), ._2(main_6__2), ._3(main_6__3),
    ._4(main_6__4), ._5(main_6__5), ._6(main_6__6), ._7(main_6__7), ._8(main_6__8), ._9(main_6__9),
    ._10(main_6__10));
  _7_Segment_Display u_7_segment_display_2 (
    .g(n7segdisp_2_g), .f(n7segdisp_2_f), .a(n7segdisp_2_a), .b(n7segdisp_2_b), .e(n7segdisp_2_e),
    .d(n7segdisp_2_d), .c(n7segdisp_2_c));  // open: dp
  buttonSenc_main main_7 (.\input (main_2_p5), .clk(clk_out), .out(main_7_out));
  LED led_2 (.in(main_2_p5));
  _7segDisp u_7segdisp_2 (
    .in_1(counter_1_q), .a(n7segdisp_2_a), .b(n7segdisp_2_b), .c(n7segdisp_2_c), .d(n7segdisp_2_d),
    .e(n7segdisp_2_e), .f(n7segdisp_2_f), .g(n7segdisp_2_g));
  Counter #(.width(3), .max('h7)) counter_1 (
    .D(3'b000), .count(main_7_out), .Q(counter_1_q), .clk(clk_out), .clr(RESET_SCORE));  // open: load, carry
  DotMatrix #(.matrixcols(10), .matrixrows(10)) dotmatrix_1 (
    .col0(main_6__1), .col1(main_6__2), .col2(main_6__3), .col3(main_6__4), .col4(main_6__5),
    .col5(main_6__6), .col6(main_6__7), .col7(main_6__8), .col8(main_6__9), .col9(main_6__10));
  buttonSenc_main main_8 (.\input (main_2_p9), .clk(clk_out), .out(main_8_out));
  _7_Segment_Display u_7_segment_display_3 (
    .g(n7segdisp_3_g), .f(n7segdisp_3_f), .a(n7segdisp_3_a), .b(n7segdisp_3_b), .e(n7segdisp_3_e),
    .d(n7segdisp_3_d), .c(n7segdisp_3_c));  // open: dp
  _7segDisp u_7segdisp_3 (
    .in_1(counter_2_q), .a(n7segdisp_3_a), .b(n7segdisp_3_b), .c(n7segdisp_3_c), .d(n7segdisp_3_d),
    .e(n7segdisp_3_e), .f(n7segdisp_3_f), .g(n7segdisp_3_g));
  Counter #(.width(3), .max('h7)) counter_2 (
    .D(3'b000), .count(main_8_out), .Q(counter_2_q), .clk(clk_out), .clr(RESET_SCORE));  // open: load, carry

  // Notes on the sheet:
  //   YOU WIN
  //   YOU LOSE
  //   COMPUTER
  //   YOU
endmodule
