// Logisim project forTTY.circ as structural Verilog: 1 circuit, main circuit main
module main (
  input  [31:0] _1,
  input  [31:0] _2,
  input  clk,
  output [7:0] outHarf
);

  wire [3:0] counter_1_q;

  Counter #(.width(4), .max('hf), .ongoal("continue")) counter_1 (
    .D(4'b0000), .count(clk), .Q(counter_1_q), .clk(clk));  // open: load, carry, clr
  Multiplexer #(.select(4), .width(8), .enable("false")) multiplexer_1 (
    .in0(_1[31:24]), .in1(_1[23:16]), .in2(_1[15:8]), .in3(_1[7:0]), .in4(_2[31:24]), .in5(_2[23:16]),
    .in6(_2[15:8]), .in7(_2[7:0]), .in8(8'hd), .in9({8{1'b0}}), .in10({8{1'b0}}), .in11({8{1'b0}}),
    .in12({8{1'b0}}), .in13({8{1'b0}}), .in14({8{1'b0}}), .in15({8{1'b0}}), .out(outHarf), .sel(counter_1_q));
endmodule
