// Logisim project harfler.circ as structural Verilog: 1 circuit, main circuit main
module main (
  input  a,
  input  b,
  input  c,
  input  d,
  input  e,
  input  f,
  input  g,
  input  h,
  input  i,
  input  j,
  input  k,
  input  l,
  input  m,
  input  n,
  input  o,
  input  p,
  input  q,
  input  r,
  input  s,
  input  t,
  input  u,
  input  v,
  input  w,
  input  x,
  input  y,
  input  z,
  input  clk,
  input  reset,
  output [7:0] harf
);

  wire priority_encoder_1_gs;
  wire [4:0] priority_encoder_1_out;
  wire [7:0] multiplexer_1_out;

  Priority_Encoder #(.select(5)) priority_encoder_1 (
    .in0(a), .in1(b), .in2(c), .in3(d), .in4(e), .in5(f), .in6(g), .in7(h), .in8(i), .in9(j), .in10(k),
    .in11(l), .in12(m), .in13(n), .in14(o), .in15(p), .in16(q), .in17(r), .in18(s), .in19(t), .in20(u),
    .in21(v), .in22(w), .in23(x), .in24(y), .in25(z), .out(priority_encoder_1_out), .gs(priority_encoder_1_gs));  // open: in26, in27, in28, in29, in30, in31, en_out, en_in
  Multiplexer #(.select(5), .width(8), .enable("false")) multiplexer_1 (
    .in0(8'h61), .in1(8'h62), .in2(8'h63), .in3(8'h64), .in4(8'h65), .in5(8'h66), .in6(8'h67), .in7(8'h68),
    .in8(8'h69), .in9(8'h6a), .in10(8'h6b), .in11(8'h6c), .in12(8'h6d), .in13(8'h6e), .in14(8'h6f),
    .in15(8'h70), .in16(8'h71), .in17(8'h72), .in18(8'h73), .in19(8'h74), .in20(8'h75), .in21(8'h76),
    .in22(8'h77), .in23(8'h78), .in24(8'h79), .in25(8'h7a), .out(multiplexer_1_out),
    .sel(priority_encoder_1_out));  // open: in26, in27, in28, in29, in30, in31
  Register register_1 (.D(multiplexer_1_out), .en(priority_encoder_1_gs), .Q(harf), .clk(clk), .clr(reset));
endmodule
